// Logisim project smips.circ as structural Verilog: 20 circuits, main circuit Board
module Board (
);

  wire CLK, HALT, MEM_WE, RESET, TTY_WE;
  wire [3:0] MEM_BE;
  wire [6:0] TTY_DATA;
  wire [31:0] MEM_ADDR, MEM_RDATA, MEM_WDATA;

  Clock Reloj (.out(CLK));
  Button u_Reset (.out(RESET));
  CPU cpu_1 (
    .CLK(CLK), .RESET(RESET), .MEM_RDATA(MEM_RDATA), .MEM_ADDR(MEM_ADDR), .MEM_WDATA(MEM_WDATA),
    .MEM_BE(MEM_BE), .MEM_WE(MEM_WE), .TTY_DATA(TTY_DATA), .TTY_WE(TTY_WE), .HALT(HALT));
  TTY #(.cols(48), .rows(12)) tty_1 (.data(TTY_DATA), .clk(CLK), .we(TTY_WE), .clr(RESET));
  Memory memory_1 (.CLK(CLK), .ADDR(MEM_ADDR), .WDATA(MEM_WDATA), .BE(MEM_BE), .WE(MEM_WE), .RDATA(MEM_RDATA));
  LED u_Halt (.in(HALT));

  // Notes on the sheet:
  //   S-MIPS | Board
  //   No modificar: la CPU se implementa dentro del subcircuito CPU.
endmodule

module CPU (
  input  CLK,
  input  RESET,
  input  [31:0] MEM_RDATA,
  output [31:0] MEM_ADDR,
  output [31:0] MEM_WDATA,
  output [3:0] MEM_BE,
  output MEM_WE,
  output [6:0] TTY_DATA,
  output TTY_WE,
  output HALT
);

  wire AddrSrc, Beq, Bne, Illegal, IRW, IsBranch, IsByte, IsLoad, IsSave, IsShift, IsWord, J, Jal, Jr, lui,
       Mem2R, PCEN, PCWrite, R2is10, RegW, Sign, SysCall, TypeI, TypeJ, TypeR, Zero;
  wire [1:0] RegASrc, RegBSrc;
  wire [2:0] AluOp, FinalAluOp;
  wire [5:0] data_path_1_funct, data_path_1_opcode;

  Data_Path data_path_1 (
    .CLK(CLK), .RST(RESET), .MemRData(MEM_RDATA), .IRWrite(IRW), .AluOp(FinalAluOp), .RegA(RegASrc),
    .RegB(RegBSrc), .RegW(RegW), .PCEN(PCEN), .Sign(Sign), .SysCall(SysCall), .PCsrc(AddrSrc),
    .IsByte(IsByte), .Mem2Reg(Mem2R), .Opcode(data_path_1_opcode), .Funct(data_path_1_funct), .Zero(Zero),
    .MemWdata(MEM_WDATA), .MemBe(MEM_BE), .LoadData(MEM_ADDR), .R2is10(R2is10), .R2is11(TTY_WE),
    .TtyData(TTY_DATA));
  ControlUnit controlunit_1 (
    .CLK(CLK), .RST(RESET), .IsShift(IsShift), .Illegal(Illegal), .Lui(lui), .IsJ(J), .IsJal(Jal),
    .IsBranch(IsBranch), .TypeR(TypeR), .TypeI(TypeI), .TypeJ(TypeJ), .IsLoad(IsLoad), .IsSave(IsSave),
    .AluOp(AluOp), .R2Is11(TTY_WE), .R2Is10(TTY_WE), .PCWrite(PCWrite), .IRWrite(IRW), .AluAsrc(RegASrc),
    .Halt(HALT), .AluBsrc(RegBSrc), .RegW(RegW), .AddrSrc(AddrSrc), .Mem2Reg(Mem2R), .FinalAluOp(FinalAluOp));
  IDecoder idecoder_1 (
    .Opcode(data_path_1_opcode), .Funct(data_path_1_funct), .IsWord(IsWord), .AluOp(AluOp), .IsByte(IsByte),
    .TypeJ(TypeJ), .TypeI(TypeI), .TypeR(TypeR), .Sign(Sign), .Jr(Jr), .IsSave(IsSave), .IsLoad(IsLoad),
    .J(J), .IsBranch(IsBranch), .Jal(Jal), .SysCall(SysCall), .IsShift(IsShift), .Illegal(Illegal),
    .Beq(Beq), .Bne(Bne), .lui(lui));
  BranchControl branchcontrol_1 (.PCWrite(PCWrite), .Beq(Beq), .Zero(Zero), .Jmp(J), .Jmr(Jr), .Bnq(Bne), .PCEN(PCEN));

  // Other names for the same wires on the sheet: Intruction[31:0] = MEM_RDATA; LoadData[31:0] = MEM_ADDR;
  //   MemBe[3:0] = MEM_BE; MemWdata[31:0] = MEM_WDATA; R2is11 = TTY_WE; RST = RESET

  // Notes on the sheet:
  //   CPU S-MIPS: implementar aqui
  //   No cambiar nombres, anchos ni sentido de los pines: la placa depende de ellos.
endmodule

module Memory (
  input  CLK,
  input  [31:0] ADDR,
  input  [31:0] WDATA,
  input  [3:0] BE,
  input  WE,
  output [31:0] RDATA
);

  RAM #(.addrWidth(12), .asyncread("true"), .byteenables("byteEnables"), .dataWidth(32), .\type ("nonvolatile")) Main_Memory (
    .addr(ADDR[13:2]), .we(WE), .oe(1'b1), .clk(CLK), .din(WDATA), .dout(RDATA), .be3(BE[3]), .be2(BE[2]),
    .be1(BE[1]), .be0(BE[0]));

  // Other names for the same wires on the sheet: A[11:0] = ADDR[13:2]

  // Notes on the sheet:
  //   Memoria unificada: 4096 palabras de 32 bits (16 KiB), little-endian
  //   Lectura combinacional; escritura en el flanco de subida de CLK con WE=1, solo en los bytes con BE=1.
  //   Se usan los bits 13..2 de ADDR; los demas se ignoran (el espacio se repite cada 16 KiB).
endmodule

module RegisterFile (
  input  RST,
  input  CLK,
  input  [31:0] DATAIN,
  input  SL,
  input  [4:0] REGA,
  input  [4:0] REGB,
  input  [4:0] REGW,
  output [31:0] AVALUE,
  output [31:0] BVALUE
);

  wire ENR1, ENR2, ENR3, ENR4, ENR5, ENR6, ENR7, ENR8, ENR9, ENR10, ENR11, ENR12, ENR13, ENR14, ENR15, ENR16,
       ENR17, ENR18, ENR19, ENR20, ENR21, ENR22, ENR23, ENR24, ENR25, ENR26, ENR27, ENR28, ENR29, ENR30,
       ENR31, LOAD;
  wire [31:0] REG0, REG1, REG2, REG3, REG4, REG5, REG6, REG7, REG8, REG9, REG10, REG11, REG12, REG13, REG14,
       REG15, REG16, REG17, REG18, REG19, REG20, REG21, REG22, REG23, REG24, REG25, REG26, REG27, REG28,
       REG29, REG30, REG31;

  not not_1 (LOAD, SL);
  Decoder #(.select(5)) decoder_1 (
    .out1(ENR1), .out2(ENR2), .out3(ENR3), .out4(ENR4), .out5(ENR5), .out6(ENR6), .out7(ENR7), .out8(ENR8),
    .out9(ENR9), .out10(ENR10), .out11(ENR11), .out12(ENR12), .out13(ENR13), .out14(ENR14), .out15(ENR15),
    .out16(ENR16), .out17(ENR17), .out18(ENR18), .out19(ENR19), .out20(ENR20), .out21(ENR21), .out22(ENR22),
    .out23(ENR23), .out24(ENR24), .out25(ENR25), .out26(ENR26), .out27(ENR27), .out28(ENR28), .out29(ENR29),
    .out30(ENR30), .out31(ENR31), .sel(REGW), .en(SL));  // open: out0
  Register #(.width(32)) register_1 (.D(DATAIN), .en(1'b0), .clk(CLK), .Q(REG0), .clr(RST));
  Register #(.width(32)) register_2 (.D(DATAIN), .en(ENR1), .clk(CLK), .Q(REG1), .clr(RST));
  Register #(.width(32)) register_3 (.D(DATAIN), .en(ENR2), .clk(CLK), .Q(REG2), .clr(RST));
  Register #(.width(32)) register_4 (.D(DATAIN), .en(ENR3), .clk(CLK), .Q(REG3), .clr(RST));
  Register #(.width(32)) register_5 (.D(DATAIN), .en(ENR4), .clk(CLK), .Q(REG4), .clr(RST));
  Register #(.width(32)) register_6 (.D(DATAIN), .en(ENR5), .clk(CLK), .Q(REG5), .clr(RST));
  Register #(.width(32)) register_7 (.D(DATAIN), .en(ENR6), .clk(CLK), .Q(REG6), .clr(RST));
  Register #(.width(32)) register_8 (.D(DATAIN), .en(ENR7), .clk(CLK), .Q(REG7), .clr(RST));
  Multiplexer #(.select(5), .width(32)) multiplexer_1 (
    .in0(REG0), .in1(REG1), .in2(REG2), .in3(REG3), .in4(REG4), .in5(REG5), .in6(REG6), .in7(REG7),
    .in8(REG8), .in9(REG9), .in10(REG10), .in11(REG11), .in12(REG12), .in13(REG13), .in14(REG14),
    .in15(REG15), .in16(REG16), .in17(REG17), .in18(REG18), .in19(REG19), .in20(REG20), .in21(REG21),
    .in22(REG22), .in23(REG23), .in24(REG24), .in25(REG25), .in26(REG26), .in27(REG27), .in28(REG28),
    .in29(REG29), .in30(REG30), .in31(REG31), .out(AVALUE), .sel(REGA));
  Register #(.width(32)) register_9 (.D(DATAIN), .en(ENR8), .clk(CLK), .Q(REG8), .clr(RST));
  Register #(.width(32)) register_10 (.D(DATAIN), .en(ENR9), .clk(CLK), .Q(REG9), .clr(RST));
  Register #(.width(32)) register_11 (.D(DATAIN), .en(ENR10), .clk(CLK), .Q(REG10), .clr(RST));
  Register #(.width(32)) register_12 (.D(DATAIN), .en(ENR11), .clk(CLK), .Q(REG11), .clr(RST));
  Register #(.width(32)) register_13 (.D(DATAIN), .en(ENR12), .clk(CLK), .Q(REG12), .clr(RST));
  Register #(.width(32)) register_14 (.D(DATAIN), .en(ENR13), .clk(CLK), .Q(REG13), .clr(RST));
  Register #(.width(32)) register_15 (.D(DATAIN), .en(ENR14), .clk(CLK), .Q(REG14), .clr(RST));
  Register #(.width(32)) register_16 (.D(DATAIN), .en(ENR15), .clk(CLK), .Q(REG15), .clr(RST));
  Multiplexer #(.select(5), .width(32)) multiplexer_2 (
    .in0(REG0), .in1(REG1), .in2(REG2), .in3(REG3), .in4(REG4), .in5(REG5), .in6(REG6), .in7(REG7),
    .in8(REG8), .in9(REG9), .in10(REG10), .in11(REG11), .in12(REG12), .in13(REG13), .in14(REG14),
    .in15(REG15), .in16(REG16), .in17(REG17), .in18(REG18), .in19(REG19), .in20(REG20), .in21(REG21),
    .in22(REG22), .in23(REG23), .in24(REG24), .in25(REG25), .in26(REG26), .in27(REG27), .in28(REG28),
    .in29(REG29), .in30(REG30), .in31(REG31), .out(BVALUE), .sel(REGB));
  Register #(.width(32)) register_17 (.D(DATAIN), .en(ENR16), .clk(CLK), .Q(REG16), .clr(RST));
  Register #(.width(32)) register_18 (.D(DATAIN), .en(ENR17), .clk(CLK), .Q(REG17), .clr(RST));
  Register #(.width(32)) register_19 (.D(DATAIN), .en(ENR18), .clk(CLK), .Q(REG18), .clr(RST));
  Register #(.width(32)) register_20 (.D(DATAIN), .en(ENR19), .clk(CLK), .Q(REG19), .clr(RST));
  Register #(.width(32)) register_21 (.D(DATAIN), .en(ENR20), .clk(CLK), .Q(REG20), .clr(RST));
  Register #(.width(32)) register_22 (.D(DATAIN), .en(ENR21), .clk(CLK), .Q(REG21), .clr(RST));
  Register #(.width(32)) register_23 (.D(DATAIN), .en(ENR22), .clk(CLK), .Q(REG22), .clr(RST));
  Register #(.width(32)) register_24 (.D(DATAIN), .en(ENR23), .clk(CLK), .Q(REG23), .clr(RST));
  Register #(.width(32)) register_25 (.D(DATAIN), .en(ENR24), .clk(CLK), .Q(REG24), .clr(RST));
  Register #(.width(32)) register_26 (.D(DATAIN), .en(ENR25), .clk(CLK), .Q(REG25), .clr(RST));
  Register #(.width(32)) register_27 (.D(DATAIN), .en(ENR26), .clk(CLK), .Q(REG26), .clr(RST));
  Register #(.width(32)) register_28 (.D(DATAIN), .en(ENR27), .clk(CLK), .Q(REG27), .clr(RST));
  Register #(.width(32)) register_29 (.D(DATAIN), .en(ENR28), .clk(CLK), .Q(REG28), .clr(RST));
  Register #(.width(32)) register_30 (.D(DATAIN), .en(ENR29), .clk(CLK), .Q(REG29), .clr(RST));
  Register #(.width(32)) register_31 (.D(DATAIN), .en(ENR30), .clk(CLK), .Q(REG30), .clr(RST));
  Register #(.width(32)) PC (.D(DATAIN), .en(ENR31), .clk(CLK), .Q(REG31), .clr(RST));

  // Other names for the same wires on the sheet: ADATA[31:0] = AVALUE; BDATA[31:0] = BVALUE; DATA[31:0] = DATAIN;
  //   SAVE = SL; SEL[4:0] = REGW
endmodule

module ALU (
  input  [31:0] A,
  input  [31:0] B,
  input  [2:0] OP,
  output [31:0] AluRes,
  output Zero
);

  wire comparator_1_eq, comparator_3_lt;
  wire [31:0] AAND, AOR, eq, NEG, neq, SHL, SHR, slt, SUB, SUM;

  Adder #(.width(32)) adder_1 (.a(A), .b(B), .out(SUM));  // open: cin, cout
  Adder #(.width(32)) adder_2 (.a(A), .b(B), .out(SUM));  // open: cin, cout
  Subtractor #(.width(32)) subtractor_1 (.a(A), .b(B), .out(SUB));  // open: bin, bout
  Negator #(.width(32)) negator_1 (.in(A), .out(NEG));
  Comparator #(.width(32)) comparator_1 (.a(A), .b(B), .eq(comparator_1_eq));  // open: gt, lt
  assign eq = {{31{comparator_1_eq}}, comparator_1_eq};  // Bit_Extender bit_extender_1
  assign neq = eq ^ 32'h1;  // XOR_Gate xor_1, 32 bits wide
  Multiplexer #(.select(3), .width(32)) multiplexer_1 (
    .in0(SUM), .in1(SUB), .in2(AAND), .in3(AOR), .in4(slt), .in5(SHL), .in6(SHR), .in7(eq), .out(AluRes),
    .sel(OP));
  // Probe on AluRes
  Comparator #(.width(32)) comparator_2 (.a(AluRes), .b({32{1'b0}}), .eq(Zero));  // open: gt, lt
  Shifter #(.width(32)) shifter_1 (.in(A), .\dist (B[4:0]), .out(SHL));
  Shifter #(.shift("lr"), .width(32)) shifter_2 (.in(A), .\dist (B[4:0]), .out(SHR));
  assign AOR = A | B;  // OR_Gate or_1, 32 bits wide
  Comparator #(.width(32)) comparator_3 (.a(A), .b(B), .lt(comparator_3_lt));  // open: gt, eq
  assign AAND = A & B;  // AND_Gate and_1, 32 bits wide
  assign slt = {{31{1'b0}}, comparator_3_lt};  // Bit_Extender bit_extender_2
endmodule

module BranchControl (
  input  PCWrite,
  input  Beq,
  input  Zero,
  input  Jmp,
  input  Jmr,
  input  Bnq,
  output PCEN
);

  wire and_1_out, and_2_out, eq;

  not not_1 (eq, Zero);
  and and_1 (and_1_out, Beq, eq);
  and and_2 (and_2_out, Bnq, Zero);
  or or_1 (PCEN, and_1_out, and_2_out, PCWrite, Jmp, Jmr);

  // Other names for the same wires on the sheet: j = Jmp; jr = Jmr; neq = Zero; pcw = PCWrite
endmodule

module IDecoder (
  input  [5:0] Opcode,
  input  [5:0] Funct,
  output IsWord,
  output [2:0] AluOp,
  output IsByte,
  output TypeJ,
  output TypeI,
  output TypeR,
  output Sign,
  output Jr,
  output IsSave,
  output IsLoad,
  output J,
  output IsBranch,
  output Jal,
  output SysCall,
  output IsShift,
  output Illegal,
  output Beq,
  output Bne,
  output lui
);

  wire addu, AluValid, and_1_out, and_2_out, and_3_out, and_4_out, and_5_out, and_6_out, and_7_out, IsAnd,
       IsOr, IsSlt, IsSum, ISum, LB, LBU, LW, not_1_out, OpAnd, OpAndi, OpOr, OpOri, OpSrl, OpSsl, or_1_out,
       or_6_out, or_7_out, or_8_out, or_9_out, or_10_out, or_11_out, or_12_out, or_13_out, or_14_out,
       or_15_out, or_18_out, or_19_out, SB, Slt, Slti, Sub, Sum, SW, TypeRValid, UISum;

  or or_1 (or_1_out, UISum, ISum);
  and and_1 (and_1_out, TypeI, or_1_out);
  and and_2 (and_2_out, OpOri, TypeI);
  and and_3 (and_3_out, TypeI, Slti);
  and and_4 (and_4_out, TypeI, OpAndi);
  GIType gitype_1 (.Opcode(Opcode), .TypeJ(TypeJ), .TypeI(TypeI), .TypeR(TypeR));
  Rtypes rtypes_1 (
    .funcode(Funct), .add(Sum), .SUB(Sub), .AAND(OpAnd), .AOR(OpOr), .SLT(Slt), .ASLL(OpSsl), .ASRL(OpSrl),
    .JR(Jr), .SYSCALL(SysCall), .addu(addu));
  Itype itype_1 (
    .OpCode(Opcode), .ADDI(ISum), .SLTI(Slti), .ANDI(OpAndi), .ORI(OpOri), .LUI(lui), .LW(LW), .ADDIU(UISum),
    .SW(SW), .LB(LB), .LBU(LBU), .SB(SB), .BEQ(Beq), .BNE(Bne));
  Jtype jtype_1 (.OpCode(Opcode), .J(J), .Jal(Jal));
  or or_2 (IsSum, Sum, addu, and_1_out);
  or or_3 (IsOr, and_2_out, OpOr);
  or or_4 (IsSlt, Slt, and_3_out);
  or or_5 (IsAnd, and_4_out, OpAnd);
  and and_5 (and_5_out, OpSsl, TypeR);
  and and_6 (and_6_out, TypeR, OpSrl);
  or or_6 (or_6_out, Sub, OpOr, Sum, OpAnd);
  or or_7 (or_7_out, OpSsl, Slt, Jr, OpSrl);
  or or_8 (or_8_out, ISum, OpAndi, OpOri, Slti);
  or or_9 (or_9_out, lui, UISum, LW, SW);
  or or_10 (or_10_out, Beq, LBU, SB, Bne);
  or or_11 (or_11_out, LB, J, Jal);
  or or_12 (or_12_out, or_8_out, or_9_out, or_10_out, or_11_out);
  ALUOpEnc aluopenc_1 (
    .sum(IsSum), .sub(Sub), .aand(IsAnd), .aor(IsOr), .slt(IsSlt), .asll(and_5_out), .asrl(and_6_out),
    .op(AluOp), .En(AluValid));
  or or_13 (or_13_out, or_6_out, SysCall, addu, or_7_out);
  not not_1 (not_1_out, TypeR);
  and and_7 (and_7_out, not_1_out, or_12_out);
  and and_8 (TypeRValid, TypeR, or_13_out);
  or or_14 (or_14_out, TypeRValid, and_7_out);
  not not_2 (Illegal, or_14_out);
  or or_15 (or_15_out, OpSsl, OpSrl);
  or or_16 (IsWord, LW, SW);
  or or_17 (IsByte, LB, LBU, SB);
  or or_18 (or_18_out, OpAndi, OpOri, LB, Slti);
  or or_19 (or_19_out, LBU, SB, Bne, Beq);
  or or_20 (IsSave, SB, SW);
  or or_21 (IsLoad, LB, LBU, LW);
  or or_22 (IsBranch, Beq, Bne);
  and and_9 (IsShift, or_15_out, TypeR);
  or or_23 (Sign, or_18_out, ISum, addu, or_19_out);

  // Other names for the same wires on the sheet: FUNCODE[5:0] = Funct
endmodule

module Rtypes (
  input  [5:0] funcode,
  output add,
  output SUB,
  output AAND,
  output AOR,
  output SLT,
  output ASLL,
  output ASRL,
  output JR,
  output SYSCALL,
  output addu
);

  Comparator #(.width(6)) comparator_1 (.a(funcode), .b(6'b100000), .eq(add));  // open: gt, lt
  Comparator #(.width(6)) comparator_2 (.a(funcode), .b(6'b100010), .eq(SUB));  // open: gt, lt
  Comparator #(.width(6)) comparator_3 (.a(funcode), .b(6'b100100), .eq(AAND));  // open: gt, lt
  Comparator #(.width(6)) comparator_4 (.a(funcode), .b(6'b100101), .eq(AOR));  // open: gt, lt
  Comparator #(.width(6)) comparator_5 (.a(funcode), .b(6'b101010), .eq(SLT));  // open: gt, lt
  Comparator #(.width(6)) comparator_6 (.a(funcode), .b({6{1'b0}}), .eq(ASLL));  // open: gt, lt
  Comparator #(.width(6)) comparator_7 (.a(funcode), .b(6'b001000), .eq(JR));  // open: gt, lt
  Comparator #(.width(6)) comparator_8 (.a(funcode), .b(6'b001100), .eq(SYSCALL));  // open: gt, lt
  Comparator #(.width(6)) comparator_9 (.a(funcode), .b(6'b000010), .eq(ASRL));  // open: gt, lt
  Comparator #(.width(6)) comparator_10 (.a(funcode), .b(6'b100001), .eq(addu));  // open: gt, lt

  // Other names for the same wires on the sheet: func[5:0] = funcode; SUM = add; USUM = addu
endmodule

module ALUOpEnc (
  input  sum,
  input  sub,
  input  aand,
  input  aor,
  input  slt,
  input  asll,
  input  asrl,
  output [2:0] op,
  output En
);

  Priority_Encoder priority_encoder_1 (
    .in0(sum), .in1(sub), .in2(aand), .in3(aor), .in4(slt), .in5(asll), .in6(asrl), .out(op), .gs(En));  // open: in7, en_in, en_out
endmodule

module GIType (
  input  [5:0] Opcode,
  output TypeJ,
  output TypeI,
  output TypeR
);

  wire comparator_1_eq, comparator_2_eq, not_1_out, not_2_out;

  Comparator #(.width(6)) comparator_1 (.a(6'b000010), .b(Opcode), .eq(comparator_1_eq));  // open: gt, lt
  Comparator #(.width(6)) comparator_2 (.a(6'b000011), .b(Opcode), .eq(comparator_2_eq));  // open: gt, lt
  Comparator #(.width(6)) comparator_3 (.a(Opcode), .b({6{1'b0}}), .eq(TypeR));  // open: gt, lt
  or or_1 (TypeJ, comparator_1_eq, comparator_2_eq);
  not not_1 (not_1_out, TypeJ);
  not not_2 (not_2_out, TypeR);
  and and_1 (TypeI, not_1_out, not_2_out);
endmodule

module Itype (
  input  [5:0] OpCode,
  output ADDI,
  output SLTI,
  output ANDI,
  output ORI,
  output LUI,
  output LW,
  output ADDIU,
  output SW,
  output LB,
  output LBU,
  output SB,
  output BEQ,
  output BNE
);

  Comparator #(.width(6)) comparator_1 (.a(OpCode), .b(6'b001000), .eq(ADDI));  // open: gt, lt
  Comparator #(.width(6)) comparator_2 (.a(OpCode), .b(6'b001010), .eq(SLTI));  // open: gt, lt
  Comparator #(.width(6)) comparator_3 (.a(OpCode), .b(6'b001100), .eq(ANDI));  // open: gt, lt
  Comparator #(.width(6)) comparator_4 (.a(OpCode), .b(6'b001101), .eq(ORI));  // open: gt, lt
  Comparator #(.width(6)) comparator_5 (.a(OpCode), .b(6'b001111), .eq(LUI));  // open: gt, lt
  Comparator #(.width(6)) comparator_6 (.a(OpCode), .b(6'b100011), .eq(LW));  // open: gt, lt
  Comparator #(.width(6)) comparator_7 (.a(OpCode), .b(6'b001001), .eq(ADDIU));  // open: gt, lt
  Comparator #(.width(6)) comparator_8 (.a(OpCode), .b(6'b101011), .eq(SW));  // open: gt, lt
  Comparator #(.width(6)) comparator_9 (.a(OpCode), .b(6'b100000), .eq(LB));  // open: gt, lt
  Comparator #(.width(6)) comparator_10 (.a(OpCode), .b(6'b100100), .eq(LBU));  // open: gt, lt
  Comparator #(.width(6)) comparator_11 (.a(OpCode), .b(6'b101000), .eq(SB));  // open: gt, lt
  Comparator #(.width(6)) comparator_12 (.a(OpCode), .b(6'b000100), .eq(BEQ));  // open: gt, lt
  Comparator #(.width(6)) comparator_13 (.a(OpCode), .b(6'b000101), .eq(BNE));  // open: gt, lt
endmodule

module Data_Path (
  input  CLK,
  input  RST,
  input  [31:0] MemRData,
  input  IRWrite,
  input  [2:0] AluOp,
  input  [1:0] RegA,
  input  [1:0] RegB,
  input  RegW,
  input  PCEN,
  input  Sign,
  input  SysCall,
  input  PCsrc,
  input  IsByte,
  input  Mem2Reg,
  output [5:0] Opcode,
  output [5:0] Funct,
  output Zero,
  output [31:0] MemWdata,
  output [3:0] MemBe,
  output [31:0] LoadData,
  output R2is10,
  output R2is11,
  output [6:0] TtyData
);

  wire [4:0] multiplexer_1_out, multiplexer_2_out;
  wire [25:6] IR;
  wire [31:0] A, Addrs, AluA, AluB, extender5b_1_evalue, IValExt, PC, PcAddrs, Result, RfileIn;
  wire [31:7] B;

  Multiplexer #(.width(5)) multiplexer_1 (.in0(IR[25:21]), .in1(5'b00010), .out(multiplexer_1_out), .sel(SysCall));
  Multiplexer #(.width(5)) multiplexer_2 (.in0(IR[20:16]), .in1(5'b00100), .out(multiplexer_2_out), .sel(SysCall));
  Multiplexer #(.width(32)) multiplexer_3 (.in0(Result), .in1(LoadData), .out(RfileIn), .sel(Mem2Reg));
  Register #(.width(32)) IReg (.D(MemRData), .en(IRWrite), .clk(CLK), .Q({Opcode, IR, Funct}), .clr(RST));
  ALU alu_1 (.A(AluA), .B(AluB), .OP(AluOp), .AluRes(Result), .Zero(Zero));
  Multiplexer #(.select(2), .width(32)) multiplexer_4 (
    .in0({B, TtyData}), .in1(32'h4), .in2(IValExt), .in3({IValExt[29:0], 2'b00}), .out(AluB), .sel(RegB));
  RegisterFile registerfile_1 (
    .RST(RST), .CLK(CLK), .DATAIN(RfileIn), .SL(RegW), .REGA(multiplexer_1_out), .REGB(multiplexer_2_out),
    .REGW(IR[15:11]), .AVALUE(A), .BVALUE({B, TtyData}));
  Extender5B extender5b_1 (.Value(IR[10:6]), .Ext(1'b0), .EValue(extender5b_1_evalue));
  Extender16B extender16b_1 (.Value({IR[15:6], Funct}), .Ext(Sign), .EValue(IValExt));
  Multiplexer #(.select(2), .width(32)) multiplexer_5 (
    .in0(A), .in1(PC), .in2(extender5b_1_evalue), .in3(32'h10), .out(AluA), .sel(RegA));
  Register #(.width(32)) register_1 (.D(PcAddrs), .en(PCEN), .clk(CLK), .Q(PC), .clr(RST));
  Multiplexer #(.width(32)) multiplexer_6 (.in0(PC), .in1(Result), .out(Addrs), .sel(Mem2Reg));
  Multiplexer #(.width(32)) multiplexer_7 (.in0(Result), .in1(PC), .out(PcAddrs), .sel(PCsrc));
  MemoryInterface memoryinterface_1 (
    .offset(Addrs[1:0]), .RTDATA({B, TtyData}), .IsByte(IsByte), .Sign(Sign), .MemRData(Addrs),
    .MemWData(MemWdata), .MemBe(MemBe), .LoadData(LoadData));
  Comparator #(.width(32)) comparator_1 (.a(A), .b(32'ha), .eq(R2is10));  // open: gt, lt
  Comparator #(.width(32)) comparator_2 (.a(A), .b(32'hb), .eq(R2is11));  // open: gt, lt

  // Other names for the same wires on the sheet: ASel[1:0] = RegA; B[6:0] = TtyData; BSel[1:0] = RegB;
  //   FUNCODE[5:0] = Funct; IR (some bits) = {Opcode, Funct}; IVAL[15:0] = {IR[15:6], Funct};
  //   JMPDEST[25:0] = {IR, Funct}; SHAMT[4:0] = IR[10:6]; RD[4:0] = IR[15:11]; RT[4:0] = IR[20:16];
  //   RS[4:0] = IR[25:21]
endmodule

module Jtype (
  input  [5:0] OpCode,
  output J,
  output Jal
);

  Comparator #(.width(6)) comparator_1 (.a(OpCode), .b(6'b000010), .eq(J));  // open: gt, lt
  Comparator #(.width(6)) comparator_2 (.a(OpCode), .b(6'b000011), .eq(Jal));  // open: gt, lt
endmodule

module MemoryInterface (
  input  [1:0] offset,
  input  [31:0] RTDATA,
  input  IsByte,
  input  Sign,
  input  [31:0] MemRData,
  output [31:0] MemWData,
  output [3:0] MemBe,
  output [31:0] LoadData
);

  wire [3:0] MemBe_t;
  wire [7:0] tmpByte;
  wire [31:0] extender8b_1_evalue;

  Decoder #(.enable("false"), .select(2)) decoder_1 (
    .out0(MemBe_t[0]), .out1(MemBe_t[1]), .out2(MemBe_t[2]), .out3(MemBe_t[3]), .sel(offset));
  Multiplexer #(.select(2), .width(8)) multiplexer_1 (
    .in0(MemRData[7:0]), .in1(MemRData[15:8]), .in2(MemRData[23:16]), .in3(MemRData[31:24]), .out(tmpByte),
    .sel(offset));
  Extender8B extender8b_1 (.Value(tmpByte), .Ext(Sign), .EValue(extender8b_1_evalue));
  Multiplexer #(.width(32)) multiplexer_2 (
    .in0(RTDATA), .in1({RTDATA[7:0], RTDATA[7:0], RTDATA[7:0], RTDATA[7:0]}), .out(MemWData), .sel(IsByte));
  Multiplexer #(.width(4)) multiplexer_3 (.in0(4'b1111), .in1(MemBe_t), .out(MemBe), .sel(IsByte));
  Multiplexer #(.width(32)) multiplexer_4 (.in0(MemRData), .in1(extender8b_1_evalue), .out(LoadData), .sel(IsByte));

  // Other names for the same wires on the sheet: B[7:0] = RTDATA[7:0]; RB1[7:0] = MemRData[7:0];
  //   RB2[7:0] = MemRData[15:8]; RB3[7:0] = MemRData[23:16]; RB4[7:0] = MemRData[31:24]
endmodule

module Extender8B (
  input  [7:0] Value,
  input  Ext,
  output [31:0] EValue
);

  wire [31:0] bit_extender_1_out, bit_extender_2_out;

  assign bit_extender_1_out = {{24{1'b0}}, Value};  // Bit_Extender bit_extender_1
  assign bit_extender_2_out = {{24{Value[7]}}, Value};  // Bit_Extender bit_extender_2
  Multiplexer #(.width(32)) multiplexer_1 (.in0(bit_extender_1_out), .in1(bit_extender_2_out), .out(EValue), .sel(Ext));
endmodule

module Extender16B (
  input  [15:0] Value,
  input  Ext,
  output [31:0] EValue
);

  wire [31:0] bit_extender_1_out, bit_extender_2_out;

  assign bit_extender_1_out = {{16{1'b0}}, Value};  // Bit_Extender bit_extender_1
  assign bit_extender_2_out = {{16{Value[15]}}, Value};  // Bit_Extender bit_extender_2
  Multiplexer #(.width(32)) multiplexer_1 (.in0(bit_extender_1_out), .in1(bit_extender_2_out), .out(EValue), .sel(Ext));
endmodule

module Extender5B (
  input  [4:0] Value,
  input  Ext,
  output [31:0] EValue
);

  wire [31:0] bit_extender_1_out, bit_extender_2_out;

  assign bit_extender_1_out = {{27{1'b0}}, Value};  // Bit_Extender bit_extender_1
  assign bit_extender_2_out = {{27{Value[4]}}, Value};  // Bit_Extender bit_extender_2
  Multiplexer #(.width(32)) multiplexer_1 (.in0(bit_extender_1_out), .in1(bit_extender_2_out), .out(EValue), .sel(Ext));
endmodule

module ControlUnit (
  input  CLK,
  input  RST,
  input  IsShift,
  input  Illegal,
  input  Lui,
  input  IsJ,
  input  IsJal,
  input  IsBranch,
  input  TypeR,
  input  TypeI,
  input  TypeJ,
  input  IsLoad,
  input  IsSave,
  input  [2:0] AluOp,
  input  R2Is11,
  input  R2Is10,
  output PCWrite,
  output IRWrite,
  output [1:0] AluAsrc,
  output Halt,
  output [1:0] AluBsrc,
  output RegW,
  output AddrSrc,
  output Mem2Reg,
  output [2:0] FinalAluOp
);

  wire and_1_out, and_2_out, and_3_out, and_4_out, and_5_out, InDecode, InHalt, InIRegState, InMemRState,
       InMemWState, InRegState, NextDecode, NextFetch, NextHalt, NextIRegState, NextMemR, NextMemW,
       NextRegState, not_1_out, not_2_out, not_4_out, or_1_out, or_2_out, or_4_out, or_5_out, or_6_out,
       or_7_out, or_8_out, or_9_out, or_10_out, or_11_out, or_12_out, undriven;
  wire [3:0] NextState, State, ToDecode, ToHalt, ToIRegState, ToMemR, ToMemW, ToRegState;

  or or_1 (or_1_out, IsSave, IsLoad);
  Register #(.width(4)) States (.D(NextState), .en(1'b1), .clk(CLK), .Q(State), .clr(RST));
  and and_1 (and_1_out, TypeI, not_1_out);
  not not_1 (not_1_out, or_1_out);
  or or_2 (or_2_out, Illegal, R2Is10);
  or or_3 (Halt, or_2_out, InHalt);
  or or_4 (or_4_out, TypeR, IsShift);
  and and_2 (and_2_out, IsLoad, InDecode);
  and and_3 (and_3_out, IsSave, InDecode);
  and and_4 (and_4_out, or_4_out, InDecode);
  and and_5 (and_5_out, and_1_out, InDecode);
  Multiplexer #(.width(4)) multiplexer_1 (.in0(4'b0000), .in1(4'b1111), .out(ToHalt), .sel(Halt));
  Multiplexer #(.width(4)) multiplexer_2 (.in0(4'b0000), .in1(4'b0001), .out(ToDecode), .sel(IRWrite));
  Multiplexer #(.width(4)) multiplexer_3 (.in0(4'b0000), .in1(4'b0010), .out(ToMemR), .sel(and_2_out));
  Multiplexer #(.width(4)) multiplexer_4 (.in0(4'b0000), .in1(4'b0011), .out(ToMemW), .sel(and_3_out));
  Multiplexer #(.width(4)) multiplexer_5 (.in0(4'b0000), .in1(4'b0100), .out(ToRegState), .sel(and_4_out));
  Multiplexer #(.width(4)) multiplexer_6 (.in0(4'b0000), .in1(4'b0101), .out(ToIRegState), .sel(and_5_out));
  StateDecoder statedecoder_1 (
    .State(State), .FetchState(IRWrite), .DecodeState(InDecode), .MemRState(InMemRState),
    .MemWState(InMemWState), .RegState(InRegState), .IRegState(InHalt), .HaltState(InIRegState));
  Comparator #(.width(4)) comparator_1 (.a(ToDecode), .b(4'b0001), .eq(NextDecode));  // open: gt, lt
  Comparator #(.width(4)) comparator_2 (.a(ToHalt), .b(4'b0001), .eq(NextHalt));  // open: gt, lt
  Comparator #(.width(4)) comparator_3 (.a(ToMemR), .b(4'b0001), .eq(NextMemR));  // open: gt, lt
  Comparator #(.width(4)) comparator_4 (.a(ToMemW), .b(4'b0001), .eq(NextMemW));  // open: gt, lt
  Comparator #(.width(4)) comparator_5 (.a(ToRegState), .b(4'b0100), .eq(NextRegState));  // open: gt, lt
  Comparator #(.width(4)) comparator_6 (.a(ToIRegState), .b(4'b0101), .eq(NextIRegState));  // open: gt, lt
  StateEncode stateencode_1 (
    .NextFetch(NextFetch), .NextDecode(NextDecode), .NextMemR(NextMemR), .NextMemW(NextMemW),
    .NextRegState(NextRegState), .NextIRegState(NextHalt), .NextHalt(NextIRegState), .NextState(NextState));
  or or_5 (or_5_out, InRegState, InIRegState);
  or or_6 (or_6_out, InRegState, InIRegState);
  or or_7 (or_7_out, NextDecode, NextMemR);
  or or_8 (or_8_out, NextMemW, NextRegState);
  or or_9 (or_9_out, NextIRegState, InHalt);
  or or_10 (or_10_out, IRWrite, or_6_out);
  or or_11 (or_11_out, or_7_out, or_8_out);
  or or_12 (or_12_out, or_11_out, or_9_out);
  not not_2 (not_2_out, IRWrite);
  Priority_Encoder #(.select(2)) priority_encoder_1 (
    .in0(or_5_out), .in1(IRWrite), .in2(undriven), .out(AluAsrc));  // open: in3, gs, en_out, en_in
  Priority_Encoder #(.select(2)) priority_encoder_2 (
    .in0(InRegState), .in1(IRWrite), .in2(TypeI), .out(AluBsrc));  // open: in3, gs, en_out, en_in
  Priority_Encoder #(.select(1)) priority_encoder_3 (.in1(or_10_out), .out(RegW));  // open: in0, gs, en_out, en_in
  not not_3 (AddrSrc, IRWrite);
  not not_4 (not_4_out, or_12_out);
  Multiplexer #(.width(3)) multiplexer_7 (.in0(AluOp), .in1(3'b000), .out(FinalAluOp), .sel(IRWrite));
  and and_6 (NextFetch, not_2_out, not_4_out);

  assign Mem2Reg = IsLoad;
  assign PCWrite = IRWrite;

  // Other names for the same wires on the sheet: InFetch = IRWrite; SyscallHalt = R2Is10; SyscallTty = R2Is11

  // Notes on the sheet:
  //   verificar que no exista halt
  //   voy a state_decode
endmodule

module StateDecoder (
  input  [3:0] State,
  output FetchState,
  output DecodeState,
  output MemRState,
  output MemWState,
  output RegState,
  output IRegState,
  output HaltState
);

  Decoder #(.enable("false"), .select(4)) decoder_1 (
    .out0(FetchState), .out1(DecodeState), .out2(MemRState), .out3(MemWState), .out4(RegState),
    .out5(IRegState), .out15(HaltState), .sel(State));  // open: out6, out7, out8, out9, out10, out11, out12, out13, out14
endmodule

module StateEncode (
  input  NextFetch,
  input  NextDecode,
  input  NextMemR,
  input  NextMemW,
  input  NextRegState,
  input  NextIRegState,
  input  NextHalt,
  output [3:0] NextState
);

  Priority_Encoder #(.select(4)) priority_encoder_1 (
    .in0(NextFetch), .in1(NextDecode), .in2(NextMemR), .in3(NextMemW), .in4(NextRegState),
    .in5(NextIRegState), .in15(NextHalt), .out(NextState));  // open: in6, in7, in8, in9, in10, in11, in12, in13, in14, gs, en_out, en_in
endmodule
